// Logisim project alu.circ as structural Verilog: 13 circuits, main circuit main
module main (
  input  [31:0] X,
  input  [31:0] Y,
  input  [3:0] Switch,
  output Signed_Overflow,
  output Equal,
  output [31:0] Result
);

  wire add_overflow, sub_overflow;
  wire [31:0] add_out, addu_out, and_out, or_out, sll_out, slt_out, sltu_out, sra_out, srl_out, sub_out,
       subu_out, xor_out;

  sll sll (.X(X), .Out(sll_out));  // open: Y
  srl srl (.X(X), .Y(Y), .Out(srl_out));
  sra sra (.X(X), .Y(Y), .Out(sra_out));
  add add (.X(X), .Y(Y), .Out(add_out), .Overflow(add_overflow));
  addu addu (.X(X), .Y(Y), .Out(addu_out));
  sub sub (.X(X), .Y(Y), .Out(sub_out), .Overflow(sub_overflow));
  subu subu (.X(X), .Y(Y), .Out(subu_out));
  \and  \and  (.X(X), .Y(Y), .Out(and_out));
  \or  \or  (.X(X), .Y(Y), .Out(or_out));
  \xor  \xor  (.X(X), .Y(Y), .Out(xor_out));
  slt slt (.X(X), .Y(Y), .Out(slt_out));
  sltu sltu (.X(X), .Y(Y), .Out(sltu_out));
  Comparator #(.width(32)) comparator_1 (.a(X), .b(Y), .eq(Equal));  // open: gt, lt
  Multiplexer #(.select(4), .width(32)) multiplexer_1 (
    .in0(sll_out), .in1(srl_out), .in2(sra_out), .in3(add_out), .in4(addu_out), .in5(sub_out),
    .in6(subu_out), .in7(and_out), .in8(or_out), .in9(xor_out), .in10(slt_out), .in11(sltu_out),
    .out(Result), .sel(Switch));  // open: in12, in13, in14, in15, en
  Multiplexer #(.select(4)) multiplexer_2 (
    .in0(1'b0), .in1(1'b0), .in2(1'b0), .in3(add_overflow), .in4(1'b0), .in5(sub_overflow), .in6(1'b0),
    .in7(1'b0), .in8(1'b0), .in9(1'b0), .in10(1'b0), .in11(1'b0), .in12(1'b0), .in13(1'b0), .in14(1'b0),
    .in15(1'b0), .out(Signed_Overflow), .sel(Switch));  // open: en

  // Other names for the same wires on the sheet: overflow = Signed_Overflow; S[3:0] = Switch

  // Notes on the sheet:
  //   INPUTS to your circuit
  //   DON'T CHANGE THE LOCATIONS OF THE INPUTS AND OUTPUTS!
  //   OUTPUTS from your circuit
endmodule

module sll (
  input  [31:0] X,
  input  [31:0] Y,
  output [31:0] Out
);

  Shifter #(.width(32)) shifter_1 (.in(Y), .\dist (X[4:0]), .out(Out));
endmodule

module srl (
  input  [31:0] X,
  input  [31:0] Y,
  output [31:0] Out
);

  Shifter #(.width(32), .shift("lr")) shifter_1 (.in(Y), .\dist (X[4:0]), .out(Out));
endmodule

module sra (
  input  [31:0] X,
  input  [31:0] Y,
  output [31:0] Out
);

  Shifter #(.width(32), .shift("ar")) shifter_1 (.in(Y), .\dist (X[4:0]), .out(Out));
endmodule

module add (
  input  [31:0] X,
  input  [31:0] Y,
  output [31:0] Out,
  output Overflow
);

  wire comparator_1_eq, comparator_2_eq, not_1_out;

  Adder #(.width(32)) adder_1 (.a(X), .b(Y), .out(Out));  // open: cin, cout
  Comparator #(.width(1)) comparator_1 (.a(Out[31]), .b(X[31]), .eq(comparator_1_eq));  // open: gt, lt
  Comparator #(.width(1)) comparator_2 (.a(X[31]), .b(Y[31]), .eq(comparator_2_eq));  // open: gt, lt
  not not_1 (not_1_out, comparator_1_eq);
  Multiplexer multiplexer_1 (.in0(1'b0), .in1(not_1_out), .out(Overflow), .sel(comparator_2_eq));  // open: en
endmodule

module addu (
  input  [31:0] X,
  input  [31:0] Y,
  output [31:0] Out
);

  Adder #(.width(32)) adder_1 (.a(X), .b(Y), .out(Out));  // open: cin, cout
endmodule

module sub (
  input  [31:0] X,
  input  [31:0] Y,
  output [31:0] Out,
  output Overflow
);

  Subtractor #(.width(32)) subtractor_1 (.a(X), .b(Y), .out(Out), .bout(Overflow));  // open: bin
endmodule

module subu (
  input  [31:0] X,
  input  [31:0] Y,
  output [31:0] Out
);

  Subtractor #(.width(32)) subtractor_1 (.a(X), .b(Y), .out(Out));  // open: bin, bout
endmodule

module \and  (
  input  [31:0] X,
  input  [31:0] Y,
  output [31:0] Out
);

  assign Out = X & Y;  // AND_Gate and_1, 32 bits wide
endmodule

module \or  (
  input  [31:0] X,
  input  [31:0] Y,
  output [31:0] Out
);

  assign Out = X | Y;  // OR_Gate or_1, 32 bits wide
endmodule

module \xor  (
  input  [31:0] X,
  input  [31:0] Y,
  output [31:0] Out
);

  assign Out = X ^ Y;  // XOR_Gate xor_1, 32 bits wide
endmodule

module slt (
  input  [31:0] X,
  input  [31:0] Y,
  output [31:0] Out
);

  wire comparator_1_lt;

  Comparator #(.width(32)) comparator_1 (.a(X), .b(Y), .lt(comparator_1_lt));  // open: gt, eq
  assign Out = {{31{1'b0}}, comparator_1_lt};  // Bit_Extender bit_extender_1
endmodule

module sltu (
  input  [31:0] X,
  input  [31:0] Y,
  output [31:0] Out
);

  wire comparator_1_lt;

  Comparator #(.width(32)) comparator_1 (.a(X), .b(Y), .lt(comparator_1_lt));  // open: gt, eq
  assign Out = {{31{1'b0}}, comparator_1_lt};  // Bit_Extender bit_extender_1
endmodule
